// Logisim project Y86 Logic Circuit.circ as structural Verilog: 6 circuits, main circuit main
module main (
  input  [63:0] in_1,
  input  [63:0] in_2,
  input  [3:0] in_3,
  input  [3:0] in_4,
  input  [3:0] in_5,
  input  in_6,
  output [63:0] out_7,
  output [63:0] out_8
);

  wire clock_1_out;

  Clock clock_1 (.out(clock_1_out));
  Decode decode_1 (
    .valE(in_1), .valM(in_2), .icode(in_3), .rA(in_4), .rB(in_5), .Write_enable(in_6), .Read_enable(in_6),
    .Clk(clock_1_out), .valA(out_7), .valB(out_8));
  Execute execute_1 ();  // open: icode, ifun, valA, valB, valC, Clk, valE, Cnd
endmodule

module RegisterFile (
  input  [63:0] W1_data,
  input  [3:0] W1_addr,
  input  W1_enable,
  input  [63:0] W2_data,
  input  [3:0] W2_addr,
  input  W2_enable,
  input  [3:0] R1_addr,
  input  R1_enable,
  input  [3:0] R2_addr,
  input  R2_enable,
  input  clk,
  output [63:0] R1_data,
  output [63:0] R2_data,
  output [63:0] rax,
  output [63:0] rcx,
  output [63:0] rdx,
  output [63:0] rbx,
  output [63:0] rsp,
  output [63:0] rbp,
  output [63:0] rsi,
  output [63:0] rdi,
  output [63:0] r8,
  output [63:0] r9,
  output [63:0] r10,
  output [63:0] r11,
  output [63:0] r12,
  output [63:0] r13,
  output [63:0] r14
);

  wire decoder_1_out0, decoder_1_out1, decoder_1_out2, decoder_1_out3, decoder_1_out4, decoder_1_out5,
       decoder_1_out6, decoder_1_out7, decoder_1_out8, decoder_1_out9, decoder_1_out10, decoder_1_out11,
       decoder_1_out12, decoder_1_out13, decoder_1_out14, decoder_1_out15, decoder_2_out0, decoder_2_out1,
       decoder_2_out2, decoder_2_out3, decoder_2_out4, decoder_2_out5, decoder_2_out6, decoder_2_out7,
       decoder_2_out8, decoder_2_out9, decoder_2_out10, decoder_2_out11, decoder_2_out12, decoder_2_out13,
       decoder_2_out14, decoder_2_out15, decoder_3_out0, decoder_3_out1, decoder_3_out2, decoder_3_out3,
       decoder_3_out4, decoder_3_out5, decoder_3_out6, decoder_3_out7, decoder_3_out8, decoder_3_out9,
       decoder_3_out10, decoder_3_out11, decoder_3_out12, decoder_3_out13, decoder_3_out14, decoder_3_out15,
       decoder_4_out0, decoder_4_out1, decoder_4_out2, decoder_4_out3, decoder_4_out4, decoder_4_out5,
       decoder_4_out6, decoder_4_out7, decoder_4_out8, decoder_4_out9, decoder_4_out10, decoder_4_out11,
       decoder_4_out12, decoder_4_out13, decoder_4_out14, decoder_4_out15, or_1_out, or_2_out, or_3_out,
       or_4_out, or_5_out, or_6_out, or_7_out, or_8_out, or_9_out, or_10_out, or_11_out, or_12_out,
       or_13_out, or_14_out, or_15_out, or_16_out;
  wire [63:0] controlled_buffer_1_out, controlled_buffer_3_out, controlled_buffer_5_out,
       controlled_buffer_7_out, controlled_buffer_9_out, controlled_buffer_11_out, controlled_buffer_13_out,
       controlled_buffer_15_out, controlled_buffer_17_out, controlled_buffer_19_out,
       controlled_buffer_21_out, controlled_buffer_23_out, controlled_buffer_25_out,
       controlled_buffer_27_out, controlled_buffer_29_out, controlled_buffer_31_out, register_16_q;

  Decoder #(.select(4)) decoder_1 (
    .out0(decoder_1_out0), .out1(decoder_1_out1), .out2(decoder_1_out2), .out3(decoder_1_out3),
    .out4(decoder_1_out4), .out5(decoder_1_out5), .out6(decoder_1_out6), .out7(decoder_1_out7),
    .out8(decoder_1_out8), .out9(decoder_1_out9), .out10(decoder_1_out10), .out11(decoder_1_out11),
    .out12(decoder_1_out12), .out13(decoder_1_out13), .out14(decoder_1_out14), .out15(decoder_1_out15),
    .sel(W1_addr), .en(W1_enable));
  Decoder #(.select(4)) decoder_2 (
    .out0(decoder_2_out0), .out1(decoder_2_out1), .out2(decoder_2_out2), .out3(decoder_2_out3),
    .out4(decoder_2_out4), .out5(decoder_2_out5), .out6(decoder_2_out6), .out7(decoder_2_out7),
    .out8(decoder_2_out8), .out9(decoder_2_out9), .out10(decoder_2_out10), .out11(decoder_2_out11),
    .out12(decoder_2_out12), .out13(decoder_2_out13), .out14(decoder_2_out14), .out15(decoder_2_out15),
    .sel(W2_addr), .en(W2_enable));
  assign controlled_buffer_1_out = decoder_1_out0 ? W1_data : 64'bz;  // Controlled_Buffer controlled_buffer_1
  assign controlled_buffer_1_out = decoder_2_out0 ? W2_data : 64'bz;  // Controlled_Buffer controlled_buffer_2
  assign controlled_buffer_3_out = decoder_1_out1 ? W1_data : 64'bz;  // Controlled_Buffer controlled_buffer_3
  assign controlled_buffer_3_out = decoder_2_out1 ? W2_data : 64'bz;  // Controlled_Buffer controlled_buffer_4
  assign controlled_buffer_5_out = decoder_1_out2 ? W1_data : 64'bz;  // Controlled_Buffer controlled_buffer_5
  assign controlled_buffer_5_out = decoder_2_out2 ? W2_data : 64'bz;  // Controlled_Buffer controlled_buffer_6
  assign controlled_buffer_7_out = decoder_1_out3 ? W1_data : 64'bz;  // Controlled_Buffer controlled_buffer_7
  assign controlled_buffer_7_out = decoder_2_out3 ? W2_data : 64'bz;  // Controlled_Buffer controlled_buffer_8
  assign controlled_buffer_9_out = decoder_1_out4 ? W1_data : 64'bz;  // Controlled_Buffer controlled_buffer_9
  assign controlled_buffer_9_out = decoder_2_out4 ? W2_data : 64'bz;  // Controlled_Buffer controlled_buffer_10
  assign controlled_buffer_11_out = decoder_1_out5 ? W1_data : 64'bz;  // Controlled_Buffer controlled_buffer_11
  assign controlled_buffer_11_out = decoder_2_out5 ? W2_data : 64'bz;  // Controlled_Buffer controlled_buffer_12
  assign controlled_buffer_13_out = decoder_1_out6 ? W1_data : 64'bz;  // Controlled_Buffer controlled_buffer_13
  assign controlled_buffer_13_out = decoder_2_out6 ? W2_data : 64'bz;  // Controlled_Buffer controlled_buffer_14
  assign controlled_buffer_15_out = decoder_1_out7 ? W1_data : 64'bz;  // Controlled_Buffer controlled_buffer_15
  assign controlled_buffer_15_out = decoder_2_out7 ? W2_data : 64'bz;  // Controlled_Buffer controlled_buffer_16
  assign controlled_buffer_17_out = decoder_1_out8 ? W1_data : 64'bz;  // Controlled_Buffer controlled_buffer_17
  assign controlled_buffer_17_out = decoder_2_out8 ? W2_data : 64'bz;  // Controlled_Buffer controlled_buffer_18
  assign controlled_buffer_19_out = decoder_1_out9 ? W1_data : 64'bz;  // Controlled_Buffer controlled_buffer_19
  assign controlled_buffer_19_out = decoder_2_out9 ? W2_data : 64'bz;  // Controlled_Buffer controlled_buffer_20
  assign controlled_buffer_21_out = decoder_1_out10 ? W1_data : 64'bz;  // Controlled_Buffer controlled_buffer_21
  assign controlled_buffer_21_out = decoder_2_out10 ? W2_data : 64'bz;  // Controlled_Buffer controlled_buffer_22
  assign controlled_buffer_23_out = decoder_1_out11 ? W1_data : 64'bz;  // Controlled_Buffer controlled_buffer_23
  assign controlled_buffer_23_out = decoder_2_out11 ? W2_data : 64'bz;  // Controlled_Buffer controlled_buffer_24
  assign controlled_buffer_25_out = decoder_1_out12 ? W1_data : 64'bz;  // Controlled_Buffer controlled_buffer_25
  assign controlled_buffer_25_out = decoder_2_out12 ? W2_data : 64'bz;  // Controlled_Buffer controlled_buffer_26
  assign controlled_buffer_27_out = decoder_1_out13 ? W1_data : 64'bz;  // Controlled_Buffer controlled_buffer_27
  assign controlled_buffer_27_out = decoder_2_out13 ? W2_data : 64'bz;  // Controlled_Buffer controlled_buffer_28
  assign controlled_buffer_29_out = decoder_1_out14 ? W1_data : 64'bz;  // Controlled_Buffer controlled_buffer_29
  assign controlled_buffer_29_out = decoder_2_out14 ? W2_data : 64'bz;  // Controlled_Buffer controlled_buffer_30
  assign controlled_buffer_31_out = decoder_1_out15 ? W1_data : 64'bz;  // Controlled_Buffer controlled_buffer_31
  assign controlled_buffer_31_out = decoder_2_out15 ? W2_data : 64'bz;  // Controlled_Buffer controlled_buffer_32
  or or_1 (or_1_out, decoder_1_out0, decoder_2_out0);
  or or_2 (or_2_out, decoder_1_out1, decoder_2_out1);
  or or_3 (or_3_out, decoder_1_out2, decoder_2_out2);
  or or_4 (or_4_out, decoder_1_out3, decoder_2_out3);
  or or_5 (or_5_out, decoder_1_out4, decoder_2_out4);
  or or_6 (or_6_out, decoder_1_out5, decoder_2_out5);
  or or_7 (or_7_out, decoder_1_out6, decoder_2_out6);
  or or_8 (or_8_out, decoder_1_out7, decoder_2_out7);
  or or_9 (or_9_out, decoder_1_out8, decoder_2_out8);
  or or_10 (or_10_out, decoder_1_out9, decoder_2_out9);
  or or_11 (or_11_out, decoder_1_out10, decoder_2_out10);
  or or_12 (or_12_out, decoder_1_out11, decoder_2_out11);
  or or_13 (or_13_out, decoder_1_out12, decoder_2_out12);
  or or_14 (or_14_out, decoder_1_out13, decoder_2_out13);
  or or_15 (or_15_out, decoder_1_out14, decoder_2_out14);
  or or_16 (or_16_out, decoder_1_out15, decoder_2_out15);
  Register #(.width(64)) register_1 (.D(controlled_buffer_1_out), .en(or_1_out), .Q(rax), .clk(clk));  // open: clr
  Register #(.width(64)) register_2 (.D(controlled_buffer_3_out), .en(or_2_out), .Q(rcx), .clk(clk));  // open: clr
  Register #(.width(64)) register_3 (.D(controlled_buffer_5_out), .en(or_3_out), .Q(rdx), .clk(clk));  // open: clr
  Register #(.width(64)) register_4 (.D(controlled_buffer_7_out), .en(or_4_out), .Q(rbx), .clk(clk));  // open: clr
  Register #(.width(64)) register_5 (.D(controlled_buffer_9_out), .en(or_5_out), .Q(rsp), .clk(clk));  // open: clr
  Register #(.width(64)) register_6 (.D(controlled_buffer_11_out), .en(or_6_out), .Q(rbp), .clk(clk));  // open: clr
  Register #(.width(64)) register_7 (.D(controlled_buffer_13_out), .en(or_7_out), .Q(rsi), .clk(clk));  // open: clr
  Register #(.width(64)) register_8 (.D(controlled_buffer_15_out), .en(or_8_out), .Q(rdi), .clk(clk));  // open: clr
  Register #(.width(64)) register_9 (.D(controlled_buffer_17_out), .en(or_9_out), .Q(r8), .clk(clk));  // open: clr
  Register #(.width(64)) register_10 (.D(controlled_buffer_19_out), .en(or_10_out), .Q(r9), .clk(clk));  // open: clr
  Register #(.width(64)) register_11 (.D(controlled_buffer_21_out), .en(or_11_out), .Q(r10), .clk(clk));  // open: clr
  Register #(.width(64)) register_12 (.D(controlled_buffer_23_out), .en(or_12_out), .Q(r11), .clk(clk));  // open: clr
  Register #(.width(64)) register_13 (.D(controlled_buffer_25_out), .en(or_13_out), .Q(r12), .clk(clk));  // open: clr
  Register #(.width(64)) register_14 (.D(controlled_buffer_27_out), .en(or_14_out), .Q(r13), .clk(clk));  // open: clr
  Register #(.width(64)) register_15 (.D(controlled_buffer_29_out), .en(or_15_out), .Q(r14), .clk(clk));  // open: clr
  Register #(.width(64)) register_16 (
    .D(controlled_buffer_31_out), .en(or_16_out), .Q(register_16_q), .clk(clk));  // open: clr
  assign R1_data = decoder_3_out0 ? rax : 64'bz;  // Controlled_Buffer controlled_buffer_33
  assign R1_data = decoder_3_out1 ? rcx : 64'bz;  // Controlled_Buffer controlled_buffer_34
  assign R1_data = decoder_3_out2 ? rdx : 64'bz;  // Controlled_Buffer controlled_buffer_35
  assign R1_data = decoder_3_out3 ? rbx : 64'bz;  // Controlled_Buffer controlled_buffer_36
  assign R1_data = decoder_3_out4 ? rsp : 64'bz;  // Controlled_Buffer controlled_buffer_37
  assign R1_data = decoder_3_out5 ? rbp : 64'bz;  // Controlled_Buffer controlled_buffer_38
  assign R1_data = decoder_3_out6 ? rsi : 64'bz;  // Controlled_Buffer controlled_buffer_39
  assign R1_data = decoder_3_out7 ? rdi : 64'bz;  // Controlled_Buffer controlled_buffer_40
  assign R1_data = decoder_3_out8 ? r8 : 64'bz;  // Controlled_Buffer controlled_buffer_41
  assign R1_data = decoder_3_out9 ? r9 : 64'bz;  // Controlled_Buffer controlled_buffer_42
  assign R1_data = decoder_3_out10 ? r10 : 64'bz;  // Controlled_Buffer controlled_buffer_43
  assign R1_data = decoder_3_out11 ? r11 : 64'bz;  // Controlled_Buffer controlled_buffer_44
  assign R1_data = decoder_3_out12 ? r12 : 64'bz;  // Controlled_Buffer controlled_buffer_45
  assign R1_data = decoder_3_out13 ? r13 : 64'bz;  // Controlled_Buffer controlled_buffer_46
  assign R1_data = decoder_3_out14 ? r14 : 64'bz;  // Controlled_Buffer controlled_buffer_47
  assign R1_data = decoder_3_out15 ? register_16_q : 64'bz;  // Controlled_Buffer controlled_buffer_48
  assign R2_data = decoder_4_out0 ? rax : 64'bz;  // Controlled_Buffer controlled_buffer_49
  assign R2_data = decoder_4_out1 ? rcx : 64'bz;  // Controlled_Buffer controlled_buffer_50
  assign R2_data = decoder_4_out2 ? rdx : 64'bz;  // Controlled_Buffer controlled_buffer_51
  assign R2_data = decoder_4_out3 ? rbx : 64'bz;  // Controlled_Buffer controlled_buffer_52
  assign R2_data = decoder_4_out4 ? rsp : 64'bz;  // Controlled_Buffer controlled_buffer_53
  assign R2_data = decoder_4_out5 ? rbp : 64'bz;  // Controlled_Buffer controlled_buffer_54
  assign R2_data = decoder_4_out6 ? rsi : 64'bz;  // Controlled_Buffer controlled_buffer_55
  assign R2_data = decoder_4_out7 ? rdi : 64'bz;  // Controlled_Buffer controlled_buffer_56
  assign R2_data = decoder_4_out8 ? r8 : 64'bz;  // Controlled_Buffer controlled_buffer_57
  assign R2_data = decoder_4_out9 ? r9 : 64'bz;  // Controlled_Buffer controlled_buffer_58
  assign R2_data = decoder_4_out10 ? r10 : 64'bz;  // Controlled_Buffer controlled_buffer_59
  assign R2_data = decoder_4_out11 ? r11 : 64'bz;  // Controlled_Buffer controlled_buffer_60
  assign R2_data = decoder_4_out12 ? r12 : 64'bz;  // Controlled_Buffer controlled_buffer_61
  assign R2_data = decoder_4_out13 ? r13 : 64'bz;  // Controlled_Buffer controlled_buffer_62
  assign R2_data = decoder_4_out14 ? r14 : 64'bz;  // Controlled_Buffer controlled_buffer_63
  assign R2_data = decoder_4_out15 ? register_16_q : 64'bz;  // Controlled_Buffer controlled_buffer_64
  Decoder #(.select(4)) decoder_3 (
    .out0(decoder_3_out0), .out1(decoder_3_out1), .out2(decoder_3_out2), .out3(decoder_3_out3),
    .out4(decoder_3_out4), .out5(decoder_3_out5), .out6(decoder_3_out6), .out7(decoder_3_out7),
    .out8(decoder_3_out8), .out9(decoder_3_out9), .out10(decoder_3_out10), .out11(decoder_3_out11),
    .out12(decoder_3_out12), .out13(decoder_3_out13), .out14(decoder_3_out14), .out15(decoder_3_out15),
    .sel(R1_addr), .en(R1_enable));
  Decoder #(.select(4)) decoder_4 (
    .out0(decoder_4_out0), .out1(decoder_4_out1), .out2(decoder_4_out2), .out3(decoder_4_out3),
    .out4(decoder_4_out4), .out5(decoder_4_out5), .out6(decoder_4_out6), .out7(decoder_4_out7),
    .out8(decoder_4_out8), .out9(decoder_4_out9), .out10(decoder_4_out10), .out11(decoder_4_out11),
    .out12(decoder_4_out12), .out13(decoder_4_out13), .out14(decoder_4_out14), .out15(decoder_4_out15),
    .sel(R2_addr), .en(R2_enable));
endmodule

module Decode (
  input  [63:0] valE,
  input  [63:0] valM,
  input  [3:0] icode,
  input  [3:0] rA,
  input  [3:0] rB,
  input  Write_enable,
  input  Read_enable,
  input  Clk,
  output [63:0] valA,
  output [63:0] valB
);

  wire and_1_out, and_2_out, and_3_out, and_4_out, decoder_1_out2, decoder_1_out3, decoder_1_out4,
       decoder_1_out5, decoder_1_out6, decoder_1_out10, decoder_1_out11, or_1_out, or_2_out, or_3_out,
       or_4_out;
  wire [3:0] multiplexer_1_out, multiplexer_2_out, multiplexer_3_out, multiplexer_4_out;

  Multiplexer #(.select(4), .width(4)) multiplexer_1 (
    .in2(rB), .in3(rB), .in6(rB), .in10(4'b0100), .in11(4'b0100), .out(multiplexer_1_out), .sel(icode));  // open: in0, in1, in4, in5, in7, in8, in9, in12, in13, in14, in15
  Multiplexer #(.select(4), .width(4)) multiplexer_2 (
    .in5(rA), .in11(rA), .out(multiplexer_2_out), .sel(icode));  // open: in0, in1, in2, in3, in4, in6, in7, in8, in9, in10, in12, in13, in14, in15
  Multiplexer #(.select(4), .width(4)) multiplexer_3 (
    .in2(rA), .in4(rA), .in5(rA), .in6(rA), .in10(rA), .in11(4'b0100), .out(multiplexer_3_out), .sel(icode));  // open: in0, in1, in3, in7, in8, in9, in12, in13, in14, in15
  Multiplexer #(.select(4), .width(4)) multiplexer_4 (
    .in4(rB), .in5(rB), .in6(rB), .in10(4'b0100), .in11(4'b0100), .out(multiplexer_4_out), .sel(icode));  // open: in0, in1, in2, in3, in7, in8, in9, in12, in13, in14, in15
  Decoder #(.enable("false"), .select(4)) decoder_1 (
    .out2(decoder_1_out2), .out3(decoder_1_out3), .out4(decoder_1_out4), .out5(decoder_1_out5),
    .out6(decoder_1_out6), .out10(decoder_1_out10), .out11(decoder_1_out11), .sel(icode));  // open: out0, out1, out7, out8, out9, out12, out13, out14, out15
  or or_1 (or_1_out, decoder_1_out2, decoder_1_out3, decoder_1_out6, decoder_1_out10, decoder_1_out11);
  or or_2 (or_2_out, decoder_1_out5, decoder_1_out11);
  or or_3 (or_3_out, decoder_1_out2, decoder_1_out4, decoder_1_out5, decoder_1_out6, decoder_1_out10, decoder_1_out11);
  or or_4 (or_4_out, decoder_1_out4, decoder_1_out5, decoder_1_out6, decoder_1_out10, decoder_1_out11);
  and and_1 (and_1_out, or_1_out, Write_enable);
  and and_2 (and_2_out, or_2_out, Write_enable);
  and and_3 (and_3_out, or_3_out, Read_enable);
  and and_4 (and_4_out, Read_enable, or_4_out);
  RegisterFile registerfile_1 (
    .W1_data(valE), .W1_addr(multiplexer_1_out), .W1_enable(and_1_out), .W2_data(valM),
    .W2_addr(multiplexer_2_out), .W2_enable(and_2_out), .R1_addr(multiplexer_3_out), .R1_enable(and_3_out),
    .R2_addr(multiplexer_4_out), .R2_enable(and_4_out), .clk(Clk), .R1_data(valA), .R2_data(valB));  // open: rax, rcx, rdx, rbx, rsp, rbp, rsi, rdi, r8, r9, r10, r11, r12, r13, r14
endmodule

module ALU (
  input  [3:0] icode,
  input  [3:0] ifun,
  input  [63:0] valB,
  input  [63:0] valA,
  input  [63:0] valC,
  output [63:0] valE
);

  wire and_2_out, comparator_1_eq, comparator_2_eq;
  wire [63:0] and_1_out, multiplexer_1_out, multiplexer_2_out, multiplexer_3_out, multiplexer_4_out,
       not_1_out, xor_1_out;

  Multiplexer #(.select(4), .width(64)) multiplexer_1 (
    .in2({64{1'b0}}), .in3({64{1'b0}}), .in4(valB), .in5(valB), .in6(valB), .in10(valB), .in11(valB),
    .out(multiplexer_1_out), .sel(icode));  // open: in0, in1, in7, in8, in9, in12, in13, in14, in15
  Multiplexer #(.select(4), .width(64)) multiplexer_2 (
    .in2(valA), .in3(valC), .in4(valC), .in5(valC), .in6(valA), .in10(64'hfffffffffffffff8), .in11(64'h8),
    .out(multiplexer_2_out), .sel(icode));  // open: in0, in1, in7, in8, in9, in12, in13, in14, in15
  assign and_1_out = multiplexer_1_out & multiplexer_2_out;  // AND_Gate and_1, 64 bits wide
  assign xor_1_out = multiplexer_1_out ^ multiplexer_2_out;  // XOR_Gate xor_1, 64 bits wide
  assign not_1_out = ~multiplexer_2_out;  // NOT_Gate not_1, 64 bits wide
  Comparator #(.mode("unsigned"), .width(4)) comparator_1 (
    .a(ifun), .b(4'b0001), .eq(comparator_1_eq));  // open: gt, lt
  Comparator #(.mode("unsigned"), .width(4)) comparator_2 (
    .a(icode), .b(4'b0110), .eq(comparator_2_eq));  // open: gt, lt
  Multiplexer #(.select(4), .width(64)) multiplexer_3 (
    .in0(multiplexer_1_out), .in1(multiplexer_1_out), .in2(and_1_out), .in3(xor_1_out),
    .out(multiplexer_3_out), .sel(ifun));  // open: in4, in5, in6, in7, in8, in9, in10, in11, in12, in13, in14, in15
  Multiplexer #(.select(4), .width(64)) multiplexer_4 (
    .in0(multiplexer_2_out), .in1(not_1_out), .in2({64{1'b0}}), .in3({64{1'b0}}), .out(multiplexer_4_out),
    .sel(ifun));  // open: in4, in5, in6, in7, in8, in9, in10, in11, in12, in13, in14, in15
  and and_2 (and_2_out, comparator_1_eq, comparator_2_eq);
  Adder #(.width(64)) adder_1 (
    .a(multiplexer_3_out), .b(multiplexer_4_out), .out(valE), .cin(and_2_out));  // open: cout
endmodule

module CC (
  input  [3:0] icode,
  input  [3:0] ifun,
  input  [63:0] valE,
  input  Clk,
  output Cnd
);

  wire and_4_out, and_5_out, and_6_out, and_7_out, and_8_out, and_9_out, comparator_1_eq, comparator_2_eq,
       comparator_2_gt, comparator_2_lt, comparator_3_eq, comparator_3_gt, comparator_3_lt, decoder_1_out0,
       decoder_1_out1, decoder_1_out2, decoder_1_out3, decoder_1_out4, decoder_1_out5, decoder_1_out6,
       or_2_out, or_3_out, or_4_out;
  wire [1:0] and_1_out, and_2_out, and_3_out, bit_extender_1_out, bit_extender_2_out, bit_extender_3_out,
       or_1_out, register_1_q;

  Comparator #(.mode("unsigned"), .width(4)) comparator_1 (
    .a(icode), .b(4'b0110), .eq(comparator_1_eq));  // open: gt, lt
  Comparator #(.width(64)) comparator_2 (
    .a(valE), .b({64{1'b0}}), .gt(comparator_2_gt), .eq(comparator_2_eq), .lt(comparator_2_lt));
  assign bit_extender_1_out = {{1{comparator_2_gt}}, comparator_2_gt};  // Bit_Extender bit_extender_1
  assign bit_extender_2_out = {{1{comparator_2_eq}}, comparator_2_eq};  // Bit_Extender bit_extender_2
  assign bit_extender_3_out = {{1{comparator_2_lt}}, comparator_2_lt};  // Bit_Extender bit_extender_3
  assign and_1_out = 2'b01 & bit_extender_1_out;  // AND_Gate and_1, 2 bits wide
  assign and_2_out = 2'b00 & bit_extender_2_out;  // AND_Gate and_2, 2 bits wide
  assign and_3_out = 2'b11 & bit_extender_3_out;  // AND_Gate and_3, 2 bits wide
  Register #(.width(2)) register_1 (.D(or_1_out), .en(comparator_1_eq), .clk(Clk), .Q(register_1_q));  // open: clr
  assign or_1_out = and_1_out | and_2_out | and_3_out;  // OR_Gate or_1, 2 bits wide
  Decoder #(.enable("false"), .select(4)) decoder_1 (
    .out0(decoder_1_out0), .out1(decoder_1_out1), .out2(decoder_1_out2), .out3(decoder_1_out3),
    .out4(decoder_1_out4), .out5(decoder_1_out5), .out6(decoder_1_out6), .sel(ifun));  // open: out7, out8, out9, out10, out11, out12, out13, out14, out15
  Comparator #(.width(2)) comparator_3 (
    .a(register_1_q), .b(2'b00), .gt(comparator_3_gt), .eq(comparator_3_eq), .lt(comparator_3_lt));
  or or_2 (or_2_out, comparator_3_eq, comparator_3_lt);
  or or_3 (or_3_out, comparator_3_gt, comparator_3_lt);
  or or_4 (or_4_out, comparator_3_gt, comparator_3_eq);
  and and_4 (and_4_out, decoder_1_out1, or_2_out);
  and and_5 (and_5_out, decoder_1_out2, comparator_3_lt);
  and and_6 (and_6_out, decoder_1_out3, comparator_3_eq);
  and and_7 (and_7_out, decoder_1_out4, or_3_out);
  and and_8 (and_8_out, decoder_1_out5, or_4_out);
  and and_9 (and_9_out, decoder_1_out6, comparator_3_gt);
  or or_5 (Cnd, decoder_1_out0, and_4_out, and_5_out, and_6_out, and_7_out, and_8_out, and_9_out);
endmodule

module Execute (
  input  [3:0] icode,
  input  [3:0] ifun,
  input  [63:0] valA,
  input  [63:0] valB,
  input  [63:0] valC,
  input  Clk,
  output [63:0] valE,
  output Cnd
);

  ALU alu_1 (.icode(icode), .ifun(ifun), .valB(valB), .valA(valA), .valC(valC), .valE(valE));
  CC cc_1 (.icode(icode), .ifun(ifun), .valE(valE), .Clk(Clk), .Cnd(Cnd));
endmodule
